// Logisim project LOGICOPERATIONSELECTOR.circ as structural Verilog: 1 circuit, main circuit main
module main (
  input  in_1,
  input  in_2,
  input  in_3,
  input  [3:0] in_4,
  input  in_5,
  input  in_6,
  output out_7
);

  wire and_1_out, and_2_out, and_3_out, and_4_out, and_5_out, and_6_out, and_7_out, and_8_out, and_9_out,
       and_10_out, and_11_out, and_12_out, and_13_out, and_14_out, and_15_out, and_16_out, and_17_out,
       and_18_out, and_19_out, decoder_1_out0, decoder_1_out1, decoder_1_out2, decoder_1_out3,
       decoder_1_out4, decoder_1_out5, decoder_1_out6, decoder_1_out7, decoder_1_out8, decoder_1_out9,
       decoder_1_out10, decoder_1_out11, decoder_1_out12, decoder_1_out13, decoder_1_out14, decoder_1_out15,
       nand_1_out, nor_1_out, not_1_out, not_2_out, not_3_out, not_4_out, not_5_out, not_6_out, or_1_out,
       or_2_out, or_3_out, xnor_1_out, xor_1_out;

  Decoder #(.select(4)) decoder_1 (
    .out0(decoder_1_out0), .out1(decoder_1_out1), .out2(decoder_1_out2), .out3(decoder_1_out3),
    .out4(decoder_1_out4), .out5(decoder_1_out5), .out6(decoder_1_out6), .out7(decoder_1_out7),
    .out8(decoder_1_out8), .out9(decoder_1_out9), .out10(decoder_1_out10), .out11(decoder_1_out11),
    .out12(decoder_1_out12), .out13(decoder_1_out13), .out14(decoder_1_out14), .out15(decoder_1_out15),
    .sel(in_4), .en(in_3));
  not not_1 (not_1_out, in_1);
  not not_2 (not_2_out, in_1);
  not not_3 (not_3_out, in_1);
  and and_1 (and_1_out, in_1, not_4_out);
  not not_4 (not_4_out, in_1);
  not not_5 (not_5_out, in_1);
  or or_1 (or_1_out, not_1_out, in_1);
  nor nor_1 (nor_1_out, in_1, in_1);
  xor xor_1 (xor_1_out, in_1, in_1);
  xnor xnor_1 (xnor_1_out, in_1, in_1);
  or or_2 (or_2_out, in_1, not_2_out);
  and and_2 (and_2_out, not_3_out, in_1);
  not not_6 (not_6_out, in_1);
  and and_3 (and_3_out, in_1, in_1);
  or or_3 (or_3_out, in_1, in_1);
  nand nand_1 (nand_1_out, in_1, in_1);
  and and_4 (and_4_out, and_3_out, decoder_1_out0);
  and and_5 (and_5_out, or_3_out, decoder_1_out1);
  and and_6 (and_6_out, decoder_1_out2, nand_1_out);
  and and_7 (and_7_out, decoder_1_out3, not_6_out);
  and and_8 (and_8_out, decoder_1_out4, not_5_out);
  and and_9 (and_9_out, decoder_1_out5, or_1_out);
  and and_10 (and_10_out, decoder_1_out6, in_5);
  and and_11 (and_11_out, decoder_1_out7, nor_1_out);
  and and_12 (and_12_out, decoder_1_out8, xor_1_out);
  and and_13 (and_13_out, decoder_1_out9, xnor_1_out);
  and and_14 (and_14_out, decoder_1_out10, or_2_out);
  and and_15 (and_15_out, decoder_1_out11, and_2_out);
  and and_16 (and_16_out, decoder_1_out12, in_6);
  and and_17 (and_17_out, decoder_1_out13, and_1_out);
  and and_18 (and_18_out, decoder_1_out14, in_1);
  and and_19 (and_19_out, decoder_1_out15, in_1);
  ExactlyOne xor_2 (
    .out(out_7), .in0(and_4_out), .in1(and_5_out), .in2(and_6_out), .in3(and_7_out), .in4(and_8_out),
    .in5(and_9_out), .in6(and_10_out), .in7(and_11_out), .in8(and_12_out), .in9(and_13_out),
    .in10(and_14_out), .in11(and_15_out), .in12(and_16_out), .in13(and_17_out), .in14(and_18_out),
    .in15(and_19_out));

  assign in_2 = in_1;

  // Notes on the sheet:
  //   B
  //   A
endmodule
